// Logisim project seq_circuit.circ as structural Verilog: 1 circuit, main circuit main
module main (
  input  X,
  input  y,
  output out_3
);

  wire and_1_out, and_2_out, clock_1_out, d_ff_1_q, or_1_out, xor_1_out;

  xor xor_1 (xor_1_out, X, y);
  and and_1 (and_1_out, X, y);
  xor xor_2 (out_3, xor_1_out, d_ff_1_q);
  and and_2 (and_2_out, xor_1_out, d_ff_1_q);
  or or_1 (or_1_out, and_2_out, and_1_out);
  Clock clock_1 (.out(clock_1_out));
  D_Flip_Flop d_ff_1 (.clk(clock_1_out), .D(or_1_out), .Q(d_ff_1_q));  // open: Qn, preset, en, reset

  // Notes on the sheet:
  //   Q
  //   C
endmodule
